// Logisim project 4x3-Registersatz.circ as structural Verilog: 2 circuits, main circuit main
module main (
  input  I0,
  input  I1,
  input  I2,
  input  A1,
  input  A0,
  input  CS,
  input  RD,
  output Q0,
  output Q1,
  output Q2
);

  wire and_1_out, and_2_out, and_3_out, and_4_out, and_5_out, and_6_out, and_7_out, and_8_out, and_9_out,
       and_10_out, and_11_out, and_12_out, and_13_out, and_14_out, and_15_out, and_16_out, and_17_out,
       and_18_out, and_19_out, and_20_out, and_21_out, and_22_out, d_ff_1_q, d_ff_2_q, d_ff_3_q, d_ff_4_q,
       d_ff_5_q, d_ff_6_q, d_ff_7_q, d_ff_8_q, d_ff_9_q, d_ff_10_q, d_ff_11_q, d_ff_12_q, not_1_out,
       not_2_out, not_3_out, not_4_out, not_5_out, not_6_out, not_7_out, not_8_out, not_9_out, not_10_out;

  not not_1 (not_1_out, CS);
  not not_2 (not_2_out, not_1_out);
  not not_3 (not_3_out, not_2_out);
  not not_4 (not_4_out, not_3_out);
  not not_5 (not_5_out, A1);
  not not_6 (not_6_out, A0);
  not not_7 (not_7_out, A1);
  not not_8 (not_8_out, A0);
  not not_9 (not_9_out, not_4_out);
  and and_1 (and_1_out, not_5_out, not_6_out);
  and and_2 (and_2_out, not_7_out, A0);
  and and_3 (and_3_out, A1, not_8_out);
  and and_4 (and_4_out, A1, A0);
  and and_5 (and_5_out, and_6_out, not_10_out);
  and and_6 (and_6_out, CS, not_9_out);
  and and_7 (and_7_out, and_1_out, and_5_out);
  and and_8 (and_8_out, and_5_out, and_2_out);
  and and_9 (and_9_out, and_3_out, and_5_out);
  and and_10 (and_10_out, and_4_out, and_5_out);
  not not_10 (not_10_out, RD);
  D_Flip_Flop d_ff_1 (.clk(and_7_out), .D(I2), .Q(d_ff_1_q));  // open: Qn, preset, en, reset
  D_Flip_Flop d_ff_2 (.clk(and_8_out), .D(I2), .Q(d_ff_2_q));  // open: Qn, preset, en, reset
  D_Flip_Flop d_ff_3 (.clk(and_9_out), .D(I2), .Q(d_ff_3_q));  // open: Qn, preset, en, reset
  and and_11 (and_11_out, d_ff_3_q, and_3_out);
  D_Flip_Flop d_ff_4 (.clk(and_10_out), .D(I2), .Q(d_ff_4_q));  // open: Qn, preset, en, reset
  and and_12 (and_12_out, d_ff_4_q, and_4_out);
  or or_1 (Q2, and_12_out, and_11_out, and_14_out, and_13_out);
  and and_13 (and_13_out, d_ff_1_q, and_1_out);
  and and_14 (and_14_out, d_ff_2_q, and_2_out);
  D_Flip_Flop d_ff_5 (.clk(and_7_out), .D(I1), .Q(d_ff_5_q));  // open: Qn, preset, en, reset
  D_Flip_Flop d_ff_6 (.clk(and_8_out), .D(I1), .Q(d_ff_6_q));  // open: Qn, preset, en, reset
  D_Flip_Flop d_ff_7 (.clk(and_9_out), .D(I1), .Q(d_ff_7_q));  // open: Qn, preset, en, reset
  and and_15 (and_15_out, d_ff_7_q, and_3_out);
  D_Flip_Flop d_ff_8 (.clk(and_10_out), .D(I1), .Q(d_ff_8_q));  // open: Qn, preset, en, reset
  and and_16 (and_16_out, d_ff_8_q, and_4_out);
  or or_2 (Q1, and_16_out, and_15_out, and_18_out, and_17_out);
  and and_17 (and_17_out, d_ff_5_q, and_1_out);
  and and_18 (and_18_out, d_ff_6_q, and_2_out);
  D_Flip_Flop d_ff_9 (.clk(and_7_out), .D(I0), .Q(d_ff_9_q));  // open: Qn, preset, en, reset
  D_Flip_Flop d_ff_10 (.clk(and_8_out), .D(I0), .Q(d_ff_10_q));  // open: Qn, preset, en, reset
  D_Flip_Flop d_ff_11 (.clk(and_9_out), .D(I0), .Q(d_ff_11_q));  // open: Qn, preset, en, reset
  D_Flip_Flop d_ff_12 (.clk(and_10_out), .D(I0), .Q(d_ff_12_q));  // open: Qn, preset, en, reset
  and and_19 (and_19_out, d_ff_12_q, and_4_out);
  or or_3 (Q0, and_19_out, and_22_out, and_21_out, and_20_out);
  and and_20 (and_20_out, d_ff_9_q, and_1_out);
  and and_21 (and_21_out, d_ff_10_q, and_2_out);
  and and_22 (and_22_out, d_ff_11_q, and_3_out);

  // Notes on the sheet:
  //   Wort 0
  //   Wort 1
  //   Wort 2
  //   Wort 3
  //   Schreibgate
  //   Wort 0
  //   Wort 1
  //   Wort 2
  //   Wort 3
endmodule

module Register (
  input  I2,
  input  I1,
  input  I0,
  input  A1,
  input  A2,
  input  CS,
  input  RD,
  output Q0,
  output Q1,
  output Q2
);

  wire and_1_out, and_2_out, and_3_out, and_4_out, and_5_out, and_6_out, and_7_out, and_8_out, and_9_out,
       and_10_out, and_11_out, and_12_out, and_13_out, and_14_out, and_15_out, and_16_out, and_17_out,
       and_18_out, and_19_out, and_20_out, and_21_out, d_ff_1_q, d_ff_2_q, d_ff_3_q, d_ff_4_q, d_ff_5_q,
       d_ff_6_q, d_ff_7_q, d_ff_8_q, d_ff_9_q, d_ff_10_q, d_ff_11_q, d_ff_12_q, not_1_out, not_2_out,
       not_3_out, not_4_out, not_5_out;

  not not_1 (not_1_out, A1);
  not not_2 (not_2_out, A2);
  not not_3 (not_3_out, A1);
  not not_4 (not_4_out, A2);
  and and_1 (and_1_out, not_1_out, not_2_out);
  and and_2 (and_2_out, not_3_out, A2);
  and and_3 (and_3_out, A1, not_4_out);
  and and_4 (and_4_out, A1, A2);
  and and_5 (and_5_out, CS, not_5_out);
  and and_6 (and_6_out, and_1_out, and_5_out);
  and and_7 (and_7_out, and_5_out, and_2_out);
  and and_8 (and_8_out, and_3_out, and_5_out);
  and and_9 (and_9_out, and_4_out, and_5_out);
  not not_5 (not_5_out, RD);
  D_Flip_Flop d_ff_1 (.clk(and_6_out), .D(I0), .Q(d_ff_1_q));  // open: Qn, preset, en, reset
  D_Flip_Flop d_ff_2 (.clk(and_7_out), .D(I0), .Q(d_ff_2_q));  // open: Qn, preset, en, reset
  D_Flip_Flop d_ff_3 (.clk(and_8_out), .D(I0), .Q(d_ff_3_q));  // open: Qn, preset, en, reset
  and and_10 (and_10_out, d_ff_3_q, and_3_out);
  D_Flip_Flop d_ff_4 (.clk(and_9_out), .D(I0), .Q(d_ff_4_q));  // open: Qn, preset, en, reset
  and and_11 (and_11_out, d_ff_4_q, and_4_out);
  or or_1 (Q2, and_11_out, and_10_out, and_13_out, and_12_out);
  and and_12 (and_12_out, d_ff_1_q, and_1_out);
  and and_13 (and_13_out, d_ff_2_q, and_2_out);
  D_Flip_Flop d_ff_5 (.clk(and_6_out), .D(I1), .Q(d_ff_5_q));  // open: Qn, preset, en, reset
  D_Flip_Flop d_ff_6 (.clk(and_7_out), .D(I1), .Q(d_ff_6_q));  // open: Qn, preset, en, reset
  D_Flip_Flop d_ff_7 (.clk(and_8_out), .D(I1), .Q(d_ff_7_q));  // open: Qn, preset, en, reset
  and and_14 (and_14_out, d_ff_7_q, and_3_out);
  D_Flip_Flop d_ff_8 (.clk(and_9_out), .D(I1), .Q(d_ff_8_q));  // open: Qn, preset, en, reset
  and and_15 (and_15_out, d_ff_8_q, and_4_out);
  or or_2 (Q1, and_15_out, and_14_out, and_17_out, and_16_out);
  and and_16 (and_16_out, d_ff_5_q, and_1_out);
  and and_17 (and_17_out, d_ff_6_q, and_2_out);
  D_Flip_Flop d_ff_9 (.clk(and_6_out), .D(I2), .Q(d_ff_9_q));  // open: Qn, preset, en, reset
  D_Flip_Flop d_ff_10 (.clk(and_7_out), .D(I2), .Q(d_ff_10_q));  // open: Qn, preset, en, reset
  D_Flip_Flop d_ff_11 (.clk(and_8_out), .D(I2), .Q(d_ff_11_q));  // open: Qn, preset, en, reset
  D_Flip_Flop d_ff_12 (.clk(and_9_out), .D(I2), .Q(d_ff_12_q));  // open: Qn, preset, en, reset
  and and_18 (and_18_out, d_ff_12_q, and_4_out);
  or or_3 (Q0, and_18_out, and_21_out, and_20_out, and_19_out);
  and and_19 (and_19_out, d_ff_9_q, and_1_out);
  and and_20 (and_20_out, d_ff_10_q, and_2_out);
  and and_21 (and_21_out, d_ff_11_q, and_3_out);

  // Notes on the sheet:
  //   Wort 0
  //   Wort 1
  //   Wort 2
  //   Wort 3
  //   Schreibgate
  //   Wort 0
  //   Wort 1
  //   Wort 2
  //   Wort 3
endmodule
